// Logisim project BancoRegistradores.circ as structural Verilog
module BancoRegistradores (
  input  [7:0] Entrada,
  input  En,
  input  Clr,
  input  [1:0] In,
  input  [1:0] Out,
  output [7:0] Saida
);

  wire Clk_out;
  wire [7:0] demultiplexer_1_out0, demultiplexer_1_out1, demultiplexer_1_out2, demultiplexer_1_out3,
       register_1_q, register_2_q, register_3_q, register_4_q;

  Clock Clk (.out(Clk_out));
  Demultiplexer #(.select(2), .width(8)) demultiplexer_1 (
    .out0(demultiplexer_1_out0), .out1(demultiplexer_1_out1), .out2(demultiplexer_1_out2),
    .out3(demultiplexer_1_out3), .in(Entrada), .sel(In), .en(En));
  Register register_1 (.D(demultiplexer_1_out0), .en(En), .Q(register_1_q), .clk(Clk_out), .clr(Clr));
  Register register_2 (.D(demultiplexer_1_out1), .en(En), .Q(register_2_q), .clk(Clk_out), .clr(Clr));
  Register register_3 (.D(demultiplexer_1_out2), .en(En), .Q(register_3_q), .clk(Clk_out));  // open: clr
  Register register_4 (.D(demultiplexer_1_out3), .en(En), .Q(register_4_q), .clk(Clk_out), .clr(Clr));
  Multiplexer #(.select(2), .width(8)) multiplexer_1 (
    .in0(register_1_q), .in1(register_2_q), .in2(register_3_q), .in3(register_4_q), .out(Saida), .sel(Out),
    .en(En));
endmodule

module BancoRegistradosRealimentacao (
  input  [7:0] Entrada,
  input  En,
  input  Clr,
  input  [1:0] In,
  input  [1:0] Out,
  output [7:0] Saida
);

  wire Clk_out;
  wire [7:0] demultiplexer_1_out0, demultiplexer_1_out1, demultiplexer_1_out2, demultiplexer_1_out3, R1_q,
       R2_q, R3_q, R4_q;

  Clock Clk (.out(Clk_out));
  Demultiplexer #(.select(2), .width(8)) demultiplexer_1 (
    .out0(demultiplexer_1_out0), .out1(demultiplexer_1_out1), .out2(demultiplexer_1_out2),
    .out3(demultiplexer_1_out3), .in(Entrada), .sel(In), .en(En));
  Register R1 (.D(demultiplexer_1_out0), .en(En), .Q(R1_q), .clk(Clk_out), .clr(Clr));
  Register R2 (.D(demultiplexer_1_out1), .en(En), .Q(R2_q), .clk(Clk_out), .clr(Clr));
  Register R3 (.D(demultiplexer_1_out2), .en(En), .Q(R3_q), .clk(Clk_out));  // open: clr
  Register R4 (.D(demultiplexer_1_out3), .en(En), .Q(R4_q), .clk(Clk_out), .clr(Clr));
  assign demultiplexer_1_out0 = R1_q;  // Buffer R1_2, 8 bits wide
  assign demultiplexer_1_out1 = R2_q;  // Buffer R2_2, 8 bits wide
  assign demultiplexer_1_out2 = R3_q;  // Buffer R3_2, 8 bits wide
  assign demultiplexer_1_out3 = R4_q;  // Buffer R4_2, 8 bits wide
  Multiplexer #(.select(2), .width(8)) multiplexer_1 (
    .in0(R1_q), .in1(R2_q), .in2(R3_q), .in3(R4_q), .out(Saida), .sel(Out), .en(En));
endmodule

module BancoRegistradoresRealimentacaoParaMuitos (
  input  [7:0] Entrada,
  input  En,
  input  Clr,
  input  [1:0] In,
  input  [1:0] Out,
  output [7:0] Saida
);

  wire undriven_2;
  wire [7:0] multiplexer_1_out, SR1, SR2, SR3, SR4, undriven;

  Clock Clk ();  // open: out
  Multiplexer #(.select(3), .width(8)) multiplexer_1 (
    .in0(Entrada), .in1(SR1), .in2(SR2), .in3(SR3), .in4(undriven), .out(multiplexer_1_out));  // open: in5, in6, in7, sel, en
  Register R1 (.D(multiplexer_1_out), .Q(SR1), .clr(undriven_2));  // open: en, clk
  Register R2 (.Q(SR2), .clr(undriven_2));  // open: D, en, clk
  Register R3 (.Q(SR3));  // open: D, en, clk, clr
  Register R4 (.Q(SR4), .clr(undriven_2));  // open: D, en, clk
  Multiplexer #(.select(2), .width(8)) multiplexer_2 (
    .in0(SR1), .in1(SR2), .in2(SR3), .in3(SR4), .out(Saida), .sel(Out), .en(undriven_2));
endmodule
