// Logisim project SomadorConversor8para16.circ as structural Verilog
module Somador (
  input  in_1,
  input  [7:0] A,
  input  [7:0] B,
  output [7:0] out_4,
  output out_5
);

  // Probe on A
  // Probe on B
  // Probe on A
  // Probe on B
  // Probe on A
  // Probe on B
  // Probe on out_4
  Adder adder_1 (.a(A), .b(B), .out(out_4), .cin(in_1), .cout(out_5));
  // Probe on out_4
  // Probe on {out_5, out_4}
  // Probe on out_4
endmodule

module _8para16 (
  input  [7:0] In8,
  input  Sign,
  output [15:0] Out16
);

  and and_1 (Out16[15], In8[7], Sign);

  assign Out16[14:0] = {{7{Out16[15]}}, In8};
endmodule

module _8para32 (
  input  [7:0] In8,
  input  in_2,
  output [31:0] Out16
);

  and and_1 (Out16[31], In8[7], in_2);

  assign Out16[30:0] = {{23{Out16[31]}}, In8};
endmodule

module _16para32 (
  input  [15:0] In8,
  input  in_2,
  output [31:0] Out16
);

  and and_1 (Out16[31], In8[15], in_2);

  assign Out16[30:0] = {{15{Out16[31]}}, In8};
endmodule
